# Fritzing sketch controlar_motor_vel_variable (saved by Fritzing 0.9.1b)
breadboards: 1

parts:
  Parte1 = Arduino Uno (Rev3)
  Q1 = NPN-Transistor [package="TO92 [THT]"]
  R1 = Resistor [tolerance=±5% resistance=220 package=THT]
  M1 = DC Motor

nets:
  N1: Parte1.D3_PWM, R1.Pin_0
  N2: Parte1.5V, Q1.C
  N3: Parte1.GND, M1.pin_2
  N4: Q1.E, M1.pin_1
  N5: Q1.B, R1.Pin_1

notes:
  Design: Ing. Nelson Peña
