# Fritzing sketch joystick1 (saved by Fritzing 0.9.3b)

parts:
  Parte1 = Thumb Joystick
  Parte2 = Arduino Uno (Rev3)

nets:
  GND: Parte1.GND, Parte2.GND
  N1: Parte1.SEL, Parte2.5V
  N2: Parte1.HORZ, Parte2.A0
  N3: Parte1.VERT, Parte2.A1
  N4: Parte1.VCC, Parte2.D7

notes:
  Valores reales utilizados
  [Gnd]-[+5v]-[VrX]-[VrY]-[Sw]
  Design: Ing. Nelson Peña
