# Fritzing sketch joystick2 (saved by Fritzing 0.9.1b)
breadboards: 1

parts:
  Parte1 = Thumb Joystick
  Parte2 = Arduino Uno (Rev3)
  LED1 = LED - 5mm [color="Green (555nm)" package="5 mm [THT]"]
  LED2 = LED - 5mm [color="White (4500K)" package="5 mm [THT]"]
  LED3 = LED - 5mm [color="Red (633nm)" package="5 mm [THT]"]
  LED4 = LED - 5mm [color="Yellow (595nm)" package="5 mm [THT]"]
  LED5 = LED - 5mm [color="Blue (430nm)" package="5 mm [THT]"]

nets:
  GND: Parte1.GND, Parte2.GND, LED1.cathode, LED2.cathode, LED3.cathode, LED4.cathode, LED5.cathode
  N1: Parte1.SEL, Parte2.5V
  N2: Parte1.HORZ, Parte2.A0
  N3: Parte1.VERT, Parte2.A1
  N4: Parte2.D8, LED5.anode
  N5: Parte2.D9_PWM, LED1.anode
  N6: Parte2.D10_PWM/SS, LED3.anode
  N7: Parte2.D11_PWM/MOSI, LED4.anode
  N8: Parte2.D12/MISO, LED2.anode

notes:
  Valores reales utilizados
  [Gnd]-[+5v]-[VrX]-[VrY]-[Sw]
  Design: Ing. Nelson Peña
  [Izquierda] - [Dererecha] - [Arriba] - [Abajo] - [Centro]
