# Fritzing sketch joystick3 (saved by Fritzing 0.9.1b)
breadboards: 1

parts:
  Parte1 = Thumb Joystick
  Parte2 = Arduino Uno (Rev3)
  LED3 = RGB LED (com. cathode, rgb) [package="5 mm [THT]"]
  R4 = Resistor [tolerance=±5% resistance=220 package=THT]
  R5 = Resistor [tolerance=±5% resistance=220 package=THT]
  R6 = Resistor [tolerance=±5% resistance=220 package=THT]

nets:
  GND: Parte1.GND, Parte2.GND
  N1: Parte1.SEL, Parte2.5V
  N2: Parte1.HORZ, Parte2.A0
  N3: Parte1.VERT, Parte2.A1
  N4: Parte2.D8, R4.Pin_1
  N5: Parte2.D9_PWM, R5.Pin_1
  N6: Parte2.D10_PWM/SS, R6.Pin_1
  N7: LED3.red_anode, R6.Pin_0
  N8: LED3.common_cathode, R5.Pin_0
  N9: LED3.blue_anode, R4.Pin_0

notes:
  Valores reales utilizados
  [Gnd]-[+5v]-[VrX]-[VrY]-[Sw]
  Design: Ing. Nelson Peña
  [Izquierda] - [Dererecha] - [Arriba] - [Abajo] - [Centro]
  [Azul] - [Rojo] - [Verde] - [Blanco] - [Apagado]
  Led Rgb Catodo Comun
